// Logisim project Computer.circ as structural Verilog: 1 circuit, main circuit main
module main (
  input  in_1,
  input  in_2,
  output out_3,
  output out_4,
  output out_5,
  output out_6,
  output syscall_2,
  output out_8,
  output w
);

  wire adder_1_cout, and_1_out, and_2_out, and_3_out, and_4_out, and_5_out, button_1_out, Clock_out,
       comparator_1_eq, comparator_2_eq, comparator_3_eq, comparator_4_eq, comparator_5_eq, comparator_6_eq,
       comparator_7_eq, comparator_8_eq, comparator_9_eq, comparator_10_eq, comparator_11_eq,
       comparator_12_eq, comparator_13_eq, comparator_14_eq, comparator_15_eq, comparator_17_eq,
       comparator_17_gt, comparator_17_lt, comparator_18_eq, comparator_19_eq, comparator_20_eq,
       comparator_21_eq, comparator_22_eq, comparator_24_eq, demultiplexer_1_out1, demultiplexer_1_out2,
       demultiplexer_1_out3, demultiplexer_1_out4, demultiplexer_1_out5, demultiplexer_1_out6,
       demultiplexer_1_out7, demultiplexer_1_out8, demultiplexer_1_out9, demultiplexer_1_out10,
       demultiplexer_1_out11, demultiplexer_1_out12, not_1_out, not_2_out, not_3_out, or_1_out, or_2_out,
       or_3_out, or_4_out, or_5_out, or_6_out, or_7_out, or_8_out, or_9_out, or_10_out, Reset_all_out,
       Running_q, Start_out, Tick_out;
  wire [1:0] priority_encoder_1_out;
  wire [3:0] Instruction_q, Instruction_q_3, Instruction_q_4, multiplexer_4_out, multiplexer_5_out,
       multiplexer_6_out, multiplexer_7_out, multiplexer_8_out, multiplexer_9_out, multiplexer_10_out,
       multiplexer_11_out, multiplexer_12_out, multiplexer_13_out, multiplexer_14_out, multiplexer_15_out,
       multiplexer_16_out, multiplexer_17_out, multiplexer_18_out, multiplexer_19_out, multiplexer_20_out,
       multiplexer_21_out, multiplexer_22_out, multiplexer_23_out, multiplexer_24_out, multiplexer_25_out,
       multiplexer_28_out;
  wire [6:0] bit_extender_1_out;
  wire [7:0] _1_q, _2_q, _3_q, _4_q, _5_q, _6_q, _7_q, _8_q, adder_1_out, adder_2_out, adder_3_out,
       bit_extender_2_out, cmp_q, controlled_buffer_1_out, multiplexer_1_out, multiplexer_2_out,
       multiplexer_3_out, multiplexer_26_out, multiplexer_27_out, multiplexer_29_out, multiplexer_30_out,
       multiplexer_31_out, multiplexer_32_out, multiplexer_33_out, multiplexer_34_out, multiplexer_35_out,
       multiplexer_36_out, multiplexer_37_out, multiplexer_38_out, negator_1_out, pc_q, sf_q, sp_q, undriven;
  wire [7:4] Instruction_q_2;
  wire [15:0] rom_1_data;

  Register #(.width(16)) Instruction (
    .D(rom_1_data), .en(1'b1), .Q({Instruction_q_4, Instruction_q_3, Instruction_q_2, Instruction_q}),
    .clk(or_2_out));  // open: clr
  Bit_Extender #(.out_width(7)) bit_extender_1 (.in(_1_q), .out(bit_extender_1_out));
  Comparator #(.width(4)) comparator_1 (.a(Instruction_q_4), .b(4'b1111), .eq(comparator_1_eq));  // open: gt, lt
  Comparator #(.width(4)) comparator_2 (.a(Instruction_q_4), .b(4'b1110), .eq(comparator_2_eq));  // open: gt, lt
  Comparator #(.width(4)) comparator_3 (.a(Instruction_q_4), .b(4'b1101), .eq(comparator_3_eq));  // open: gt, lt
  Comparator #(.width(4)) comparator_4 (.a(Instruction_q_4), .b(4'b1100), .eq(comparator_4_eq));  // open: gt, lt
  Comparator #(.width(4)) comparator_5 (.a(Instruction_q_4), .b(4'b1011), .eq(comparator_5_eq));  // open: gt, lt
  Comparator #(.width(4)) comparator_6 (.a(Instruction_q_4), .b(4'b1010), .eq(comparator_6_eq));  // open: gt, lt
  Comparator #(.width(4)) comparator_7 (.a(Instruction_q_4), .b(4'b1001), .eq(comparator_7_eq));  // open: gt, lt
  Comparator #(.width(4)) comparator_8 (.a(Instruction_q_4), .b(4'b1000), .eq(comparator_8_eq));  // open: gt, lt
  Comparator #(.width(4)) comparator_9 (.a(Instruction_q_4), .b(4'b0111), .eq(comparator_9_eq));  // open: gt, lt
  Comparator #(.width(4)) comparator_10 (.a(Instruction_q_4), .b(4'b0110), .eq(comparator_10_eq));  // open: gt, lt
  Comparator #(.width(4)) comparator_11 (.a(Instruction_q_4), .b(4'b0101), .eq(comparator_11_eq));  // open: gt, lt
  Comparator #(.width(4)) comparator_12 (.a(Instruction_q_4), .b(4'b0100), .eq(comparator_12_eq));  // open: gt, lt
  Comparator #(.width(4)) comparator_13 (.a(Instruction_q_4), .b(4'b0011), .eq(comparator_13_eq));  // open: gt, lt
  Comparator #(.width(4)) comparator_14 (.a(Instruction_q_4), .b(4'b0010), .eq(comparator_14_eq));  // open: gt, lt
  Comparator #(.width(4)) comparator_15 (.a(Instruction_q_4), .b(4'b0001), .eq(comparator_15_eq));  // open: gt, lt
  Comparator #(.width(4)) comparator_16 (.a(Instruction_q_4), .b(4'b0000), .eq(w));  // open: gt, lt
  TTY tty_1 (.data(bit_extender_1_out), .clk(or_2_out), .we(comparator_24_eq), .clr(Reset_all_out));
  ROM #(.dataWidth(16)) rom_1 (.addr(pc_q), .data(rom_1_data), .sel(1'b1));
  Button Start (.out(Start_out));
  Button button_1 (.out(button_1_out));
  or or_1 (or_1_out, button_1_out, comparator_21_eq);
  Register #(.width(1)) Running (.D(Start_out), .en(Start_out), .Q(Running_q), .clk(Start_out), .clr(or_1_out));
  Clock Clock (.out(Clock_out));
  and and_1 (and_1_out, Running_q, Clock_out);
  or or_2 (or_2_out, and_1_out, Tick_out);
  Button Tick (.out(Tick_out));
  Multiplexer #(.select(4), .width(8), .disabled(0), .enable("false")) multiplexer_1 (
    .in0({8{1'b0}}), .in1(_1_q), .in2(_2_q), .in3(_3_q), .in4(_4_q), .in5(_5_q), .in6(_6_q), .in7(_7_q),
    .in8(_8_q), .in9(cmp_q), .in10(sp_q), .in11(sf_q), .in12(pc_q), .in13({8{1'b0}}), .in14({8{1'b0}}),
    .in15({8{1'b0}}), .out(multiplexer_1_out), .sel(multiplexer_7_out));
  Register _1 (.D(multiplexer_36_out), .en(demultiplexer_1_out1), .Q(_1_q), .clk(or_2_out), .clr(or_3_out));
  Button Reset_all (.out(Reset_all_out));
  Register _2 (.D(multiplexer_36_out), .en(demultiplexer_1_out2), .Q(_2_q), .clk(or_2_out), .clr(or_3_out));
  buf or_3 (or_3_out, Reset_all_out);  // OR_Gate
  Register _3 (.D(multiplexer_36_out), .en(demultiplexer_1_out3), .Q(_3_q), .clk(or_2_out), .clr(or_3_out));
  Register _4 (.D(multiplexer_36_out), .en(demultiplexer_1_out4), .Q(_4_q), .clk(or_2_out), .clr(or_3_out));
  Register _5 (.D(multiplexer_36_out), .en(demultiplexer_1_out5), .Q(_5_q), .clk(or_2_out), .clr(or_3_out));
  Register _6 (.D(multiplexer_36_out), .en(demultiplexer_1_out6), .Q(_6_q), .clk(or_2_out), .clr(or_3_out));
  Register _7 (.D(multiplexer_36_out), .en(demultiplexer_1_out7), .Q(_7_q), .clk(or_2_out), .clr(or_3_out));
  Demultiplexer #(.select(4), .disabled(0), .enable("false")) demultiplexer_1 (
    .out0(out_3), .out1(demultiplexer_1_out1), .out2(demultiplexer_1_out2), .out3(demultiplexer_1_out3),
    .out4(demultiplexer_1_out4), .out5(demultiplexer_1_out5), .out6(demultiplexer_1_out6),
    .out7(demultiplexer_1_out7), .out8(demultiplexer_1_out8), .out9(demultiplexer_1_out9),
    .out10(demultiplexer_1_out10), .out11(demultiplexer_1_out11), .out12(demultiplexer_1_out12),
    .out13(out_4), .out14(out_5), .out15(out_6), .in(1'b1), .sel(multiplexer_17_out));
  Register _8 (.D(multiplexer_36_out), .en(demultiplexer_1_out8), .Q(_8_q), .clk(or_2_out), .clr(Reset_all_out));
  Register cmp (.D(multiplexer_36_out), .en(demultiplexer_1_out9), .Q(cmp_q), .clk(or_2_out), .clr(or_3_out));
  Register sp (.D(multiplexer_36_out), .en(demultiplexer_1_out10), .Q(sp_q), .clk(or_2_out), .clr(or_3_out));
  Register sf (.D(multiplexer_36_out), .en(demultiplexer_1_out11), .Q(sf_q), .clk(or_2_out), .clr(or_3_out));
  Multiplexer #(.width(8), .enable("false")) multiplexer_2 (
    .in0(adder_1_out), .in1(multiplexer_36_out), .out(multiplexer_2_out), .sel(demultiplexer_1_out12));
  Register pc (.D(multiplexer_2_out), .en(1'b1), .Q(pc_q), .clk(or_2_out), .clr(Reset_all_out));
  Multiplexer #(.select(4), .width(8), .disabled(0), .enable("false")) multiplexer_3 (
    .in0({8{1'b0}}), .in1(_1_q), .in2(_2_q), .in3(_3_q), .in4(_4_q), .in5(_5_q), .in6(_6_q), .in7(_7_q),
    .in8(_8_q), .in9(cmp_q), .in10(sp_q), .in11(sf_q), .in12(pc_q), .in13({8{1'b0}}), .in14({8{1'b0}}),
    .in15({8{1'b0}}), .out(multiplexer_3_out), .sel(multiplexer_13_out));
  Adder adder_1 (.a(8'h1), .b(pc_q), .out(adder_1_out), .cout(adder_1_cout));  // open: cin
  LED Program_Overflowed_ROM (.in(adder_1_cout));
  assign controlled_buffer_1_out = not_2_out ? multiplexer_1_out : 8'bz;  // Controlled_Buffer controlled_buffer_1
  not not_1 (not_1_out, not_2_out);
  or or_4 (or_4_out, comparator_4_eq, comparator_3_eq, comparator_2_eq, comparator_1_eq);
  not not_2 (not_2_out, or_6_out);
  RAM #(.bus("asynch")) ram_1 (
    .addr(multiplexer_37_out), .data(controlled_buffer_1_out), .sel(or_7_out), .ld(not_1_out),
    .clr(Reset_all_out));
  Multiplexer #(.width(4), .enable("false")) multiplexer_4 (
    .in0(multiplexer_5_out), .in1(Instruction_q_3), .out(multiplexer_4_out), .sel(comparator_6_eq));
  Multiplexer #(.width(4), .enable("false")) multiplexer_5 (
    .in0(multiplexer_6_out), .in1(Instruction_q_3), .out(multiplexer_5_out), .sel(comparator_5_eq));
  Multiplexer #(.width(4), .enable("false")) multiplexer_6 (
    .in0(4'b0000), .in1(4'b1001), .out(multiplexer_6_out), .sel(or_4_out));
  Multiplexer #(.width(4), .enable("false")) multiplexer_7 (
    .in0(multiplexer_8_out), .in1(Instruction_q_2), .out(multiplexer_7_out), .sel(comparator_13_eq));
  Multiplexer #(.width(4), .enable("false")) multiplexer_8 (
    .in0(multiplexer_9_out), .in1(Instruction_q_3), .out(multiplexer_8_out), .sel(comparator_12_eq));
  Multiplexer #(.width(4), .enable("false")) multiplexer_9 (
    .in0(multiplexer_10_out), .in1(Instruction_q_3), .out(multiplexer_9_out), .sel(comparator_11_eq));
  Multiplexer #(.width(4), .enable("false")) multiplexer_10 (
    .in0(multiplexer_11_out), .in1(Instruction_q_3), .out(multiplexer_10_out), .sel(comparator_9_eq));
  Multiplexer #(.width(4), .enable("false")) multiplexer_11 (
    .in0(multiplexer_4_out), .in1(4'b1000), .out(multiplexer_11_out), .sel(comparator_8_eq));
  Multiplexer #(.width(4), .enable("false")) multiplexer_12 (
    .in0(4'b0000), .in1(Instruction_q_2), .out(multiplexer_12_out), .sel(comparator_5_eq));
  Multiplexer #(.width(4), .enable("false")) multiplexer_13 (
    .in0(multiplexer_14_out), .in1(Instruction_q_2), .out(multiplexer_13_out), .sel(comparator_15_eq));
  Multiplexer #(.width(4), .enable("false")) multiplexer_14 (
    .in0(multiplexer_15_out), .in1(Instruction_q_3), .out(multiplexer_14_out), .sel(comparator_13_eq));
  Multiplexer #(.width(4), .enable("false")) multiplexer_15 (
    .in0(multiplexer_16_out), .in1(Instruction_q_2), .out(multiplexer_15_out), .sel(comparator_10_eq));
  Multiplexer #(.width(4), .enable("false")) multiplexer_16 (
    .in0(multiplexer_12_out), .in1(Instruction_q_2), .out(multiplexer_16_out), .sel(comparator_9_eq));
  Adder adder_2 (.a(multiplexer_3_out), .b(multiplexer_1_out), .out(adder_2_out));  // open: cin, cout
  Adder adder_3 (.a({Instruction_q_2, Instruction_q}), .b(multiplexer_1_out), .out(adder_3_out));  // open: cin, cout
  Negator negator_1 (.in(multiplexer_1_out), .out(negator_1_out));
  Comparator comparator_17 (
    .a(multiplexer_1_out), .b(multiplexer_3_out), .gt(comparator_17_gt), .eq(comparator_17_eq),
    .lt(comparator_17_lt));
  Multiplexer #(.width(4), .enable("false")) multiplexer_17 (
    .in0(multiplexer_28_out), .in1(Instruction_q_3), .out(multiplexer_17_out), .sel(comparator_15_eq));
  Multiplexer #(.width(4), .enable("false")) multiplexer_18 (
    .in0(multiplexer_19_out), .in1(Instruction_q_3), .out(multiplexer_18_out), .sel(comparator_13_eq));
  Multiplexer #(.width(4), .enable("false")) multiplexer_19 (
    .in0(multiplexer_20_out), .in1(Instruction_q_3), .out(multiplexer_19_out), .sel(comparator_12_eq));
  Multiplexer #(.width(4), .enable("false")) multiplexer_20 (
    .in0(multiplexer_21_out), .in1(Instruction_q_3), .out(multiplexer_20_out), .sel(comparator_11_eq));
  Multiplexer #(.width(4), .enable("false")) multiplexer_21 (
    .in0(multiplexer_22_out), .in1(Instruction_q_3), .out(multiplexer_21_out), .sel(comparator_10_eq));
  Multiplexer #(.width(4), .enable("false")) multiplexer_22 (
    .in0(multiplexer_23_out), .in1(4'b1100), .out(multiplexer_22_out), .sel(comparator_7_eq));
  Multiplexer #(.width(4), .enable("false")) multiplexer_23 (
    .in0(multiplexer_24_out), .in1(4'b1100), .out(multiplexer_23_out), .sel(comparator_6_eq));
  Multiplexer #(.width(4), .enable("false")) multiplexer_24 (
    .in0(multiplexer_25_out), .in1(4'b1001), .out(multiplexer_24_out), .sel(comparator_5_eq));
  Multiplexer #(.width(4), .enable("false")) multiplexer_25 (
    .in0(4'b0000), .in1(4'b1100), .out(multiplexer_25_out), .sel(or_4_out));
  Multiplexer #(.width(8), .enable("false")) multiplexer_26 (
    .in0(undriven), .in1({Instruction_q_3, Instruction_q_2}), .out(multiplexer_26_out), .sel(or_5_out));
  Multiplexer #(.width(8), .enable("false")) multiplexer_27 (
    .in0(multiplexer_29_out), .in1({Instruction_q_2, Instruction_q}), .out(multiplexer_27_out),
    .sel(comparator_14_eq));
  Multiplexer #(.width(4), .enable("false")) multiplexer_28 (
    .in0(multiplexer_18_out), .in1(Instruction_q_3), .out(multiplexer_28_out), .sel(comparator_14_eq));
  Multiplexer #(.width(8), .enable("false")) multiplexer_29 (
    .in0(multiplexer_30_out), .in1(adder_2_out), .out(multiplexer_29_out), .sel(comparator_13_eq));
  Multiplexer #(.width(8), .enable("false")) multiplexer_30 (
    .in0(multiplexer_31_out), .in1(adder_3_out), .out(multiplexer_30_out), .sel(comparator_12_eq));
  Multiplexer #(.width(8), .enable("false")) multiplexer_31 (
    .in0(multiplexer_32_out), .in1(negator_1_out), .out(multiplexer_31_out), .sel(comparator_11_eq));
  Multiplexer #(.width(8), .enable("false")) multiplexer_32 (
    .in0(multiplexer_33_out), .in1(controlled_buffer_1_out), .out(multiplexer_32_out), .sel(comparator_10_eq));
  Multiplexer #(.width(8), .enable("false")) multiplexer_33 (
    .in0(multiplexer_34_out), .in1({Instruction_q_3, Instruction_q_2}), .out(multiplexer_33_out),
    .sel(comparator_7_eq));
  Multiplexer #(.width(8), .enable("false")) multiplexer_34 (
    .in0(multiplexer_35_out), .in1(multiplexer_1_out), .out(multiplexer_34_out), .sel(comparator_6_eq));
  Multiplexer #(.width(8), .enable("false")) multiplexer_35 (
    .in0(multiplexer_26_out), .in1(bit_extender_2_out), .out(multiplexer_35_out), .sel(comparator_5_eq));
  Multiplexer #(.width(8), .enable("false")) multiplexer_36 (
    .in0(multiplexer_27_out), .in1(multiplexer_3_out), .out(multiplexer_36_out), .sel(comparator_15_eq));
  Priority_Encoder #(.select(2), .disabled(0)) priority_encoder_1 (
    .in0(1'b1), .in1(comparator_17_gt), .in2(comparator_17_eq), .in3(comparator_17_lt),
    .out(priority_encoder_1_out));  // open: gs, en_out, en_in
  Comparator comparator_18 (.a(multiplexer_1_out), .b(8'h1), .eq(comparator_18_eq));  // open: gt, lt
  Comparator comparator_19 (.a(multiplexer_1_out), .b(8'h2), .eq(comparator_19_eq));  // open: gt, lt
  Comparator comparator_20 (.a(multiplexer_1_out), .b(8'h3), .eq(comparator_20_eq));  // open: gt, lt
  Multiplexer #(.width(8), .enable("false")) multiplexer_37 (
    .in0(multiplexer_3_out), .in1(multiplexer_3_out), .out(multiplexer_37_out), .sel(comparator_10_eq));
  assign bit_extender_2_out = {{6{1'b0}}, priority_encoder_1_out};  // Bit_Extender bit_extender_2
  and and_2 (and_2_out, comparator_19_eq, comparator_4_eq);
  or or_5 (or_5_out, and_2_out, or_8_out);
  or or_6 (or_6_out, 1'b0, comparator_10_eq);
  or or_7 (or_7_out, comparator_10_eq, or_9_out);
  or or_8 (or_8_out, and_3_out, or_10_out);
  or or_9 (or_9_out, comparator_9_eq, 1'b0);
  and and_3 (and_3_out, comparator_18_eq, comparator_2_eq);
  or or_10 (or_10_out, and_4_out, and_5_out);
  Multiplexer #(.width(8), .enable("false")) multiplexer_38 (
    .in0({8{1'b0}}), .in1(multiplexer_1_out), .out(multiplexer_38_out), .sel(comparator_8_eq));
  not not_3 (not_3_out, comparator_19_eq);
  and and_4 (and_4_out, comparator_20_eq, comparator_3_eq);
  Comparator comparator_21 (.a(multiplexer_38_out), .b(8'hf), .eq(comparator_21_eq));  // open: gt, lt
  Comparator comparator_22 (.a(multiplexer_38_out), .b(8'h3), .eq(comparator_22_eq));  // open: gt, lt
  Comparator comparator_23 (.a(multiplexer_38_out), .b(8'h2), .eq(syscall_2));  // open: gt, lt
  Comparator comparator_24 (.a(multiplexer_38_out), .b(8'h1), .eq(comparator_24_eq));  // open: gt, lt
  Comparator comparator_25 (.a(multiplexer_38_out), .b({8{1'b0}}), .eq(out_8));  // open: gt, lt
  and and_5 (and_5_out, not_3_out, comparator_1_eq);

  // Notes on the sheet:
  //   Arguments
  //   Opcode
  //   Designed by Radu Vasilescu
  //   For instruction set reference, see `Instruction Set.txt`
  //   An assembler, written in Python, is available in `assemble.py`
  //   8-Bit Computer
  //   $1
  //   jne
  //   jgt
  //   jlt
  //   jeq
  //   cmp
  //   ja
  //   j
  //   syscall
  //   sw
  //   lw
  //   neg
  //   addi
  //   add
  //   li
  //   mov
  //   nop
  //   program counter
  //   clock
  //   r
  //   d
  //   w
  //   d
  //   r
  //   w
  //   r
  //   d
  //   w
  //   d
  //   r
  //   w
  //   rr
  //   a
  //   w
  //   r
  //   w
  //   r
  //   w
  //   r
  //   w?
  //   rr
  //   m
  //   r
  //   m
  //   w
  //   a
  //   r
  //   w
  //   a
  //   r
  //   w
  //   a
  //   r
  //   w
  //   w
  //   r
  //   opcode
  //   arg1
  //   arg2
  //   last 4 bits
  //   last 8 bits
  //   first 8 bits
  //   Program
  //   Clock
  //   0 0 0 0
  //   0 0 0 0
  //   ^
  //   |
  //   overlaps with
  //   contents of rom_1 (hex, n*v repeats v):
  //   2131 2200 2305 2801 8000 4101 4201 b230 d030 c0a0 280f 8000
  //   Output
  //   0 0 0 0
  //   0 0 0 0
  //   jump address AKA Middle byte
  //   stop clock
  //   0 0 0 0 
  //   or
  //   register read id
  //   register read value
  //   syscall ff
  //   syscall 1
  //   0 0 0 0 
  //   SKIP
  //   SKIP
  //   $0
  //   0 0 0 0   0 0 0 0 
  //   syscall 3
  //   register write value
  //   register write id
  //   Registers
  //   default = $pc + 1
  //   $pc + 1
  //   but if "enabled" = 1 --> use reg data in
  //   register read id
  //   register read value
  //   j
  //   jump address
  //   reset all button
  //   Conditionals
  //   jeq
  //   jlt
  //   jgt
  //   jne
  //   Register Ops.
  //   Arithmetic
  //   RAM Access
  //   Jumps
  //   ja
  //   conditional jump
  //   RAM
  //   addi
  //   neg
  //   lw
  //   sw
  //   syscall
  //   cmp
  //   mov
  //   arg1
  //   arg2
  //   li
  //   the byte
  //   add
  //   id
  //   arg2
  //   arg1
  //   arg1
  //   arg1
  //   store?
  //   value
  //   arg1
  //   store data
  //   load data
  //   1 = read, 0 = store
  //   id
  //   arg2
  //   arg2
  //   value
  //   the byte
  //   value of reg
  //   jump address
  //   the value to li
  //   the address in which to li
  //   id
  //   arg1
  //   arg1
  //   pc
  //   pc
  //   pc
  //   $cmp
  //   Should we jump?
  //   value
  //   $cmp values:
  //   1: arg1 > arg2
  //   2: arg1 = arg2
  //   3: arg1 < arg2
  //   address
  //   load/read data
  //   >
  //   =
  //   <
  //   jeq
  //   jlt
  //   jgt
  //   jne
  //   1 = read
  //   0 = store
  //   ld
  //   ram enabled
  //   nop
  //   value of $8
  //   AKA Syscall #
  //   Syscalls
  //   /
  //   |
  //   OR
  //   |
  //   \
  //   We should jump if:
  //   jeq AND =
  //   jgt AND >
  //   jlt AND <
  //   jne AND NOT =
endmodule
